# Fritzing sketch fc-03 tachometer (saved by Fritzing 0.9.3b)
breadboards: 1

parts:
  FC-03 = FC-03 [chip_label=FC-03]
  Arduino_UNO = Arduino Uno (Rev3)

nets:
  VCC: FC-03.VCC, Arduino_UNO.3V3
  GND: FC-03.GND, Arduino_UNO.GND
  N1: FC-03.A0, Arduino_UNO.D2

custom parts:
  FC-03: FC-03, LM393 IR Speed Sensor Encoder
